# Fritzing sketch button_pullUp_pullDown (saved by Fritzing 1.0.1rc)
circuit board: 5.23238cm x 5.37303cm
breadboards: 1

parts:
  NodeMCU = Amica NodeMCU DEVKIT 1.0
  R1 = Resistor [tolerance=±5% power=0.25W resistance=220 package=THT]
  R2 = Resistor [tolerance=±5% power=0.25W resistance=220 package=THT]
  Pull_Down_Button = Pushbutton [package="[THT]"]
  Pull_Up_Button = Pushbutton [package="[THT]"]
  LED_Sinking = smd LED [color="Red (633nm)" package="1206 [SMD]"]
  LED_Sourcing = smd LED [color="Red (633nm)" package="1206 [SMD]"]
  R3 = Resistor [tolerance=±5% power=0.25W resistance=10k package=THT]

nets:
  N1: NodeMCU.pin1, NodeMCU.pin_10, NodeMCU.pin_26, R1.Pin_1, Pull_Down_Button.Pin_1, Pull_Down_Button.Pin_2
  N2: NodeMCU.pin2, NodeMCU.pin_9, NodeMCU.pin_25, NodeMCU.pin_29, Pull_Up_Button.Pin_3, Pull_Up_Button.Pin_4, LED_Sourcing.cathode, R3.Pin_0
  N3: NodeMCU.pin7, Pull_Down_Button.Pin_3, Pull_Down_Button.Pin_4, R3.Pin_1
  N4: NodeMCU.pin8, Pull_Up_Button.Pin_1, Pull_Up_Button.Pin_2
  N5: NodeMCU.pin_13, R2.Pin_0
  N6: NodeMCU.pin_14, LED_Sinking.cathode
  N7: R1.Pin_0, LED_Sinking.anode
  N8: R2.Pin_1, LED_Sourcing.anode
