# Fritzing sketch external_led_sinking_sourcing (saved by Fritzing 1.0.1rc)
circuit board: 5.23238cm x 5.37303cm
breadboards: 1

parts:
  NodeMCU = Amica NodeMCU DEVKIT 1.0
  LED_Sinking = smd LED [color="Red (633nm)" package="1206 [SMD]"]
  LED_Sourcing = smd LED [color="Red (633nm)" package="1206 [SMD]"]
  R1 = Resistor [tolerance=±5% power=0.25W resistance=220 package=THT]
  R2 = Resistor [tolerance=±5% power=0.25W resistance=220 package=THT]

nets:
  N1: NodeMCU.pin1, NodeMCU.pin_10, NodeMCU.pin_26, R1.Pin_0
  N2: NodeMCU.pin2, NodeMCU.pin_9, NodeMCU.pin_25, NodeMCU.pin_29, LED_Sourcing.cathode
  N3: NodeMCU.pin_13, R2.Pin_0
  N4: NodeMCU.pin_14, LED_Sinking.cathode
  N5: LED_Sinking.anode, R1.Pin_1
  N6: LED_Sourcing.anode, R2.Pin_1
